# Fritzing sketch BatterieScrufe (saved by Fritzing 1.0.4)
circuit board: 1.57277cm x 4.1942cm
breadboards: 1

parts:
  J1 = screw terminal, 6 pins

nets:
  N1: J1.pin1, J1.pin3
  N2: J1.pin2, J1.pin5
  N3: J1.pin4, J1.pin6

notes:
  +  -  +  -  +  -
  B1
  B2
  Ex
