# Fritzing sketch Verbinder (saved by Fritzing 0.9.10b)
circuit board: 1cm x 1cm
breadboards: 1

parts:
  J1 = female pin header, 3 pins [form="♀ (female)"]
  J2 = female pin header, 3 pins [form="♀ (female)"]

nets:
  N1: J1.pin1, J1.pin2, J1.pin3, J2.pin1, J2.pin2, J2.pin3
